# Fritzing sketch ESP32_LED_RGB_forJake (saved by Fritzing 0.9.3b)
breadboards: 1

parts:
  Part2 = Adafruit HUZZAH32 ESP32 Feather [part_number="Adafruit #3405"]
  LED2 = RGB LED (com. cathode, rgb) [package="5 mm [THT]"]
  R1 = Resistor [tolerance=±1% resistance=430 package=THT]
  R2 = Resistor [tolerance=±1% resistance=430 package=THT]
  R3 = Resistor [tolerance=±1% resistance=470 package=THT]

nets:
  N1: Part2.GND, LED2.common_cathode
  N2: Part2.IO12_A11, R3.Pin_0
  N3: Part2.IO27_A10, R1.Pin_0
  N4: Part2.IO33_A9, R2.Pin_0
  N5: LED2.red_anode, R3.Pin_1
  N6: LED2.green_anode, R1.Pin_1
  N7: LED2.blue_anode, R2.Pin_1
